# Fritzing sketch Arduino Garage Parking Assist (saved by Fritzing 0.9.2b)
breadboards: 2

parts:
  Part1 = Arduino Nano (Rev3.0)
  J2 = male pin header, 2 pins [form="♂ (male)"]
  J1 = male pin header, 3 pins [form="♂ (male)"]
  J3 = Screw terminal - 2 pins [package=THT]
  J4 = Screw terminal - 2 pins [package=THT]
  J5 = Screw terminal - 2 pins [package=THT]
  J7 = Screw terminal - 2 pins [package=THT]
  J6 = double row male pin header, 2 pins [form="♂ (male)"]
  Part6 = Adafruit VL53L0X Time of Flight Distance Sensor [part_number="Adafruit #3317"]

nets:
  N1: Part1.GND, J3.pin1, J4.pin2, J5.pin1
  N2: Part1.D10, J1.pin3
  N3: Part1.D11/MOSI, J1.pin2
  N4: Part1.D12/MISO, J1.pin1
  N5: Part1.VIN, J3.pin2, J4.pin1, J5.pin2
  N6: Part1.A5, J2.pin1
  N7: Part1.A4, J2.pin2
  N8: J7.pin1, Part6.GND
  N9: J7.pin2, Part6.VIN
  N10: J6.pin1, Part6.SDA
  N11: J6.pin2, Part6.SCL

notes:
  Signal to R, Y, G Light Relays
  To Sensor
  5v Power in
  Relay power
  Sensor power
  Garage Parking Assistant
  To Power J5
  To Arduino J2

custom parts:
  Adafruit VL53L0X Time of Flight Distance Sensor: The VL53L0X is a Time of Flight distance sensor like no other you've used! The sensor contains a very tiny invisible laser source, and a matching sensor. The VL53L0X can detect the "time of flight", or how long the light has taken to bounce back to the sensor. Since it uses a very narrow light source, it is good for determining distance of only the surface directly in front of it. Unlike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
